// Logisim project NAND gate.circ as structural Verilog: 1 circuit, main circuit main
module main (
  input  input0,
  input  input1,
  output output0
);

  wire transistor_4_out;

  Transistor transistor_1 (.in(1'b1), .out(output0), .gate(input1));
  Transistor transistor_2 (.in(1'b1), .out(output0), .gate(input0));
  Transistor #(.\type ("n")) transistor_3 (.in(transistor_4_out), .out(output0), .gate(input0));
  Transistor #(.\type ("n")) transistor_4 (.in(1'b0), .out(transistor_4_out), .gate(input1));
endmodule
