// Logisim project NOR gate.circ as structural Verilog: 1 circuit, main circuit main
module main (
  input  input0,
  input  input1,
  output output0
);

  wire transistor_1_out;

  Transistor transistor_1 (.in(1'b1), .out(transistor_1_out), .gate(input0));
  Transistor transistor_2 (.in(transistor_1_out), .out(output0), .gate(input1));
  Transistor #(.\type ("n")) transistor_3 (.in(1'b0), .out(output0), .gate(input0));
  Transistor #(.\type ("n")) transistor_4 (.in(1'b0), .out(output0), .gate(input1));
endmodule
