// Logisim project Transmission gate.circ as structural Verilog: 1 circuit, main circuit main
module main (
  input  input_Control,
  input  input_A,
  input  input_ControlC,
  input  input_X,
  output output_B,
  output output_Y
);

  wire transistor_1_out, transistor_3_out;

  Transistor transistor_1 (.in(1'b1), .out(transistor_1_out), .gate(input_Control));
  Transistor #(.\type ("n")) transistor_2 (.in(1'b0), .out(transistor_1_out), .gate(input_Control));
  Transistor transistor_3 (.in(1'b1), .out(transistor_3_out), .gate(input_ControlC));
  Transistor #(.\type ("n")) transistor_4 (.in(1'b0), .out(transistor_3_out), .gate(input_ControlC));
  Transistor transistor_5 (.in(input_A), .out(output_B), .gate(transistor_1_out));
  Transistor #(.\type ("n")) transistor_6 (.in(input_A), .out(output_B), .gate(input_Control));
  Transistor transistor_7 (.in(input_X), .out(output_Y), .gate(transistor_3_out));
  Transistor #(.\type ("n")) transistor_8 (.in(input_X), .out(output_Y), .gate(input_ControlC));

  // Notes on the sheet:
  //   Drains as output
  //   Sources as output
  //   P
endmodule
