// Logisim project XNOR gate.circ as structural Verilog: 1 circuit, main circuit main
module main (
  input  input0,
  input  inputA,
  input  inputB,
  input  input1,
  input  inputX,
  input  inputY,
  output outputY,
  output output0,
  output outputA
);

  wire transistor_1_out, transistor_3_out, transistor_9_out, transistor_11_out, transistor_17_out,
       transistor_19_out;

  Transistor transistor_1 (.in(inputA), .out(transistor_1_out), .gate(inputB));
  Transistor #(.\type ("n")) transistor_2 (.in(transistor_9_out), .out(transistor_1_out), .gate(inputB));
  Transistor transistor_3 (.in(inputX), .out(transistor_3_out), .gate(inputY));
  Transistor #(.\type ("n")) transistor_4 (.in(transistor_11_out), .out(transistor_3_out), .gate(inputY));
  Transistor transistor_5 (.in(inputB), .out(transistor_1_out), .gate(inputA));
  Transistor #(.\type ("n")) transistor_6 (.in(inputB), .out(transistor_1_out), .gate(transistor_9_out));
  Transistor transistor_7 (.in(inputY), .out(transistor_3_out), .gate(inputX));
  Transistor #(.\type ("n")) transistor_8 (.in(inputY), .out(transistor_3_out), .gate(transistor_11_out));
  Transistor transistor_9 (.in(1'b1), .out(transistor_9_out), .gate(inputA));
  Transistor #(.\type ("n")) transistor_10 (.in(1'b0), .out(transistor_9_out), .gate(inputA));
  Transistor transistor_11 (.in(1'b1), .out(transistor_11_out), .gate(inputX));
  Transistor #(.\type ("n")) transistor_12 (.in(1'b0), .out(transistor_11_out), .gate(inputX));
  Transistor transistor_13 (.in(1'b1), .out(outputY), .gate(transistor_1_out));
  Transistor #(.\type ("n")) transistor_14 (.in(1'b0), .out(outputY), .gate(transistor_1_out));
  Transistor transistor_15 (.in(1'b1), .out(outputA), .gate(transistor_3_out));
  Transistor #(.\type ("n")) transistor_16 (.in(1'b0), .out(outputA), .gate(transistor_3_out));
  Transistor transistor_17 (.in(1'b1), .out(transistor_17_out), .gate(input0));
  Transistor #(.\type ("n")) transistor_18 (.in(1'b0), .out(transistor_17_out), .gate(input0));
  Transistor transistor_19 (.in(input0), .out(transistor_19_out), .gate(input1));
  Transistor #(.\type ("n")) transistor_20 (.in(transistor_17_out), .out(transistor_19_out), .gate(input1));
  Transistor transistor_21 (.in(input1), .out(transistor_19_out), .gate(input0));
  Transistor #(.\type ("n")) transistor_22 (.in(input1), .out(transistor_19_out), .gate(transistor_17_out));
  Transistor transistor_23 (.in(1'b1), .out(output0), .gate(transistor_19_out));
  Transistor #(.\type ("n")) transistor_24 (.in(1'b0), .out(output0), .gate(transistor_19_out));

  // Notes on the sheet:
  //   Transimission Gate lay down
endmodule
