// Logisim project XOR gate.circ as structural Verilog: 1 circuit, main circuit main
module main (
  input  input0,
  input  inputA,
  input  inputB,
  input  input1,
  input  inputX,
  input  inputY,
  output outputY,
  output output0,
  output outputA
);

  wire transistor_9_out, transistor_11_out, transistor_13_out;

  Transistor transistor_1 (.in(inputA), .out(outputY), .gate(inputB));
  Transistor #(.\type ("n")) transistor_2 (.in(transistor_9_out), .out(outputY), .gate(inputB));
  Transistor transistor_3 (.in(inputX), .out(outputA), .gate(inputY));
  Transistor #(.\type ("n")) transistor_4 (.in(transistor_11_out), .out(outputA), .gate(inputY));
  Transistor transistor_5 (.in(inputB), .out(outputY), .gate(inputA));
  Transistor #(.\type ("n")) transistor_6 (.in(inputB), .out(outputY), .gate(transistor_9_out));
  Transistor transistor_7 (.in(inputY), .out(outputA), .gate(inputX));
  Transistor #(.\type ("n")) transistor_8 (.in(inputY), .out(outputA), .gate(transistor_11_out));
  Transistor transistor_9 (.in(1'b1), .out(transistor_9_out), .gate(inputA));
  Transistor #(.\type ("n")) transistor_10 (.in(1'b0), .out(transistor_9_out), .gate(inputA));
  Transistor transistor_11 (.in(1'b1), .out(transistor_11_out), .gate(inputX));
  Transistor #(.\type ("n")) transistor_12 (.in(1'b0), .out(transistor_11_out), .gate(inputX));
  Transistor transistor_13 (.in(1'b1), .out(transistor_13_out), .gate(input0));
  Transistor #(.\type ("n")) transistor_14 (.in(1'b0), .out(transistor_13_out), .gate(input0));
  Transistor transistor_15 (.in(input0), .out(output0), .gate(input1));
  Transistor #(.\type ("n")) transistor_16 (.in(transistor_13_out), .out(output0), .gate(input1));
  Transistor transistor_17 (.in(input1), .out(output0), .gate(input0));
  Transistor #(.\type ("n")) transistor_18 (.in(input1), .out(output0), .gate(transistor_13_out));

  // Notes on the sheet:
  //   Transimission Gate lay down
endmodule
